// Logisim project driver_module.circ as structural Verilog: 1 circuit, main circuit main
// Z
module main (
  input  CE,
  input  CLK,
  input  DEC,
  input  [2:0] SL
);

  wire and_1_out, demultiplexer_1_out0, demultiplexer_1_out1, demultiplexer_2_out0, demultiplexer_2_out1,
       demultiplexer_3_out0, demultiplexer_3_out1, demultiplexer_3_out2, n74193_1_pin1, n74193_1_pin2,
       n74193_1_pin3, n74193_1_pin4, n74193_1_pin5, n74193_1_pin6, n74193_1_pin7, n74193_1_pin9,
       n74193_1_pin10, n74193_1_pin11, n74193_1_pin14, n74193_1_pin15, n74193_2_pin1, n74193_2_pin2,
       n74193_2_pin3, n74193_2_pin6, n74193_2_pin7, n74193_2_pin9, n74193_2_pin10, n74193_2_pin15,
       n74193_3_pin1, n74193_3_pin2, n74193_3_pin4, n74193_3_pin5, n74193_3_pin9, n74193_3_pin10,
       n74193_3_pin11, n74193_3_pin14, n74193_3_pin15, n74193_4_pin1, n74193_4_pin4, n74193_4_pin5,
       n74193_4_pin9, n74193_4_pin10, n74193_4_pin15, n74193_5_pin1, n74193_5_pin4, n74193_5_pin5,
       n74193_5_pin9, n74193_5_pin10, n74193_5_pin15, n74193_6_pin1, n74193_6_pin9, n74193_6_pin10,
       n74193_6_pin15, nor_1_out, or_1_out, or_2_out;

  and and_1 (and_1_out, CE, CLK);
  _74193 #(.ShowInternalStructure("true")) u_74193_1 (
    .pin1(n74193_1_pin1), .pin2(n74193_1_pin2), .pin3(n74193_1_pin3), .pin4(n74193_1_pin4),
    .pin5(n74193_1_pin5), .pin6(n74193_1_pin6), .pin7(n74193_1_pin7), .pin15(n74193_1_pin15),
    .pin14(n74193_1_pin14), .pin11(n74193_1_pin11), .pin10(n74193_1_pin10), .pin9(n74193_1_pin9));  // open: pin13, pin12
  Demultiplexer demultiplexer_1 (.out0(demultiplexer_1_out0), .out1(demultiplexer_1_out1), .in(and_1_out), .sel(DEC));
  Demultiplexer demultiplexer_2 (.out0(demultiplexer_2_out0), .out1(demultiplexer_2_out1), .in(CLK), .sel(DEC));
  or or_1 (or_1_out, demultiplexer_1_out0, demultiplexer_2_out1);
  or or_2 (or_2_out, demultiplexer_2_out0, demultiplexer_1_out1);
  _74193 #(.ShowInternalStructure("true")) u_74193_2 (
    .pin1(n74193_2_pin1), .pin2(n74193_2_pin2), .pin3(n74193_2_pin3), .pin6(n74193_2_pin6),
    .pin7(n74193_2_pin7), .pin15(n74193_2_pin15), .pin14(n74193_1_pin14), .pin13(n74193_1_pin4),
    .pin12(n74193_1_pin5), .pin11(n74193_1_pin11), .pin10(n74193_2_pin10), .pin9(n74193_2_pin9));  // open: pin4, pin5
  LedBar ledbar_1 (
    .led0(n74193_1_pin7), .led1(n74193_1_pin6), .led2(n74193_1_pin2), .led3(n74193_1_pin3),
    .led4(n74193_2_pin7), .led5(n74193_2_pin6), .led6(n74193_2_pin2), .led7(n74193_2_pin3));
  nor nor_1 (nor_1_out, n74193_1_pin7, n74193_1_pin6, n74193_1_pin2, n74193_1_pin3, n74193_2_pin7, n74193_2_pin6, n74193_2_pin2, n74193_2_pin3);
  LED Z (.in(nor_1_out));
  Demultiplexer #(.select(3)) demultiplexer_3 (
    .out0(demultiplexer_3_out0), .out1(demultiplexer_3_out1), .out2(demultiplexer_3_out2), .in(or_1_out),
    .sel(SL));  // open: out3, out4, out5, out6, out7
  Demultiplexer #(.select(3)) demultiplexer_4 (
    .out0(demultiplexer_3_out0), .out1(demultiplexer_3_out1), .out2(demultiplexer_3_out2), .in(or_2_out),
    .sel(SL));  // open: out3, out4, out5, out6, out7
  _74193 #(.ShowInternalStructure("true")) u_74193_3 (
    .pin1(n74193_3_pin1), .pin2(n74193_3_pin2), .pin3(n74193_3_pin2), .pin4(n74193_3_pin4),
    .pin5(n74193_3_pin5), .pin6(n74193_3_pin2), .pin7(n74193_3_pin2), .pin15(n74193_3_pin15),
    .pin14(n74193_3_pin14), .pin11(n74193_3_pin11), .pin10(n74193_3_pin10), .pin9(n74193_3_pin9));  // open: pin13, pin12
  _74193 #(.ShowInternalStructure("true")) u_74193_4 (
    .pin1(n74193_4_pin1), .pin2(n74193_3_pin2), .pin3(n74193_3_pin2), .pin4(n74193_4_pin4),
    .pin5(n74193_4_pin5), .pin6(n74193_3_pin2), .pin7(n74193_3_pin2), .pin15(n74193_4_pin15),
    .pin14(n74193_3_pin14), .pin13(n74193_3_pin4), .pin12(n74193_3_pin5), .pin11(n74193_3_pin11),
    .pin10(n74193_4_pin10), .pin9(n74193_4_pin9));
  _74193 #(.ShowInternalStructure("true")) u_74193_5 (
    .pin1(n74193_5_pin1), .pin2(n74193_3_pin2), .pin3(n74193_3_pin2), .pin4(n74193_5_pin4),
    .pin5(n74193_5_pin5), .pin6(n74193_3_pin2), .pin7(n74193_3_pin2), .pin15(n74193_5_pin15),
    .pin14(n74193_3_pin14), .pin13(n74193_4_pin4), .pin12(n74193_4_pin5), .pin11(n74193_3_pin11),
    .pin10(n74193_5_pin10), .pin9(n74193_5_pin9));
  LedBar #(.matrixcols(16)) ledbar_2 (
    .led0(n74193_3_pin2), .led1(n74193_3_pin2), .led2(n74193_3_pin2), .led3(n74193_3_pin2),
    .led4(n74193_3_pin2), .led5(n74193_3_pin2), .led6(n74193_3_pin2), .led7(n74193_3_pin2),
    .led8(n74193_3_pin2), .led9(n74193_3_pin2), .led10(n74193_3_pin2), .led11(n74193_3_pin2),
    .led12(n74193_3_pin2), .led13(n74193_3_pin2), .led14(n74193_3_pin2), .led15(n74193_3_pin2));
  _74193 #(.ShowInternalStructure("true")) u_74193_6 (
    .pin1(n74193_6_pin1), .pin2(n74193_3_pin2), .pin3(n74193_3_pin2), .pin6(n74193_3_pin2),
    .pin7(n74193_3_pin2), .pin15(n74193_6_pin15), .pin14(n74193_3_pin14), .pin13(n74193_5_pin4),
    .pin12(n74193_5_pin5), .pin11(n74193_3_pin11), .pin10(n74193_6_pin10), .pin9(n74193_6_pin9));  // open: pin4, pin5

  // Notes on the sheet:
  //   REGISTER MODULE
  //   LOAD
  //   RESET
  //   COMMON INTERFACE
  //   8-BIT STORED DATA | DATA OUT
  //   74LS193
  //   UP
  //   DOWN
  //   8-BIT DATA IN
  //   LEDs
  //   74LS193
  //   SELECT INTERFACE
  //   REGISTER 1
  //   REGISTER 2
  //   REGISTER 3
  //   ...
  //   REGISTER N
  //   LOAD
  //   RESET
  //   74LS193
  //   74LS193
  //   74LS193
  //   16-BIT STORED DATA | DATA OUT
  //   16-BIT DATA IN
  //   LEDs
  //   BUT DATA OUT/IN
  //   E
  //   DIR
  //   BUS TRANSCEIVER
  //   BUT DATA OUT/IN
endmodule
