// Logisim project clock_divider.circ as structural Verilog: 1 circuit, main circuit main
module main (
);

  wire n7404_1_pin5, n7404_1_pin9, n7404_1_pin11, n7404_1_pin13, n7408_1_pin1, n7408_1_pin2, n7408_1_pin3,
       n7408_1_pin5, n7408_1_pin6, n7408_1_pin8, n7408_1_pin9, n7408_1_pin11, n7408_1_pin12, n74138_1_pin1,
       n74138_1_pin2, n74138_1_pin4, n74138_1_pin5, n74138_1_pin6, n74138_1_pin11, n74161_1_pin1,
       n74161_1_pin7, n74161_1_pin9, n74161_1_pin10, n74161_1_pin11, n74161_1_pin12, n74161_1_pin13,
       n74161_1_pin14, n74161_2_pin7, n74161_2_pin9, n74161_2_pin10;
  wire [3:0] n74161_1_pin3;

  LED led_1 (.in(n7408_1_pin11));
  LED led_2 (.in(n7408_1_pin8));
  LED led_3 (.in(n7408_1_pin3));
  LED led_4 (.in(n7408_1_pin6));
  _7408 u_7408_1 (
    .pin1(n7408_1_pin1), .pin2(n7408_1_pin2), .pin3(n7408_1_pin3), .pin4(n7408_1_pin1), .pin5(n7408_1_pin5),
    .pin6(n7408_1_pin6), .pin13(n7408_1_pin1), .pin12(n7408_1_pin12), .pin11(n7408_1_pin11),
    .pin10(n7408_1_pin1), .pin9(n7408_1_pin9), .pin8(n7408_1_pin8));
  LedBar #(.matrixcols(4)) ledbar_1 (
    .led0(n74161_1_pin11), .led1(n74161_1_pin12), .led2(n74161_1_pin13), .led3(n74161_1_pin14));
  _74161 u_74161_1 (
    .pin1(n74161_1_pin1), .pin2(n7408_1_pin11), .pin3(n74161_1_pin3[0]), .pin4(n74161_1_pin3[1]),
    .pin5(n74161_1_pin3[2]), .pin6(n74161_1_pin3[3]), .pin7(n74161_1_pin7), .pin14(n74161_1_pin14),
    .pin13(n74161_1_pin13), .pin12(n74161_1_pin12), .pin11(n74161_1_pin11), .pin10(n74161_1_pin10),
    .pin9(n74161_1_pin9));  // open: pin15
  _7404 u_7404_1 (
    .pin5(n7404_1_pin5), .pin6(n7408_1_pin5), .pin13(n7404_1_pin13), .pin12(n7408_1_pin12),
    .pin11(n7404_1_pin11), .pin10(n7408_1_pin9), .pin9(n7404_1_pin9), .pin8(n7408_1_pin2));  // open: pin1, pin2, pin3, pin4
  _74138 u_74138_1 (
    .pin1(n74138_1_pin1), .pin2(n74138_1_pin2), .pin4(n74138_1_pin4), .pin5(n74138_1_pin5),
    .pin6(n74138_1_pin6), .pin15(n7404_1_pin13), .pin14(n7404_1_pin11), .pin13(n7404_1_pin9),
    .pin12(n7404_1_pin5), .pin11(n74138_1_pin11));  // open: pin3, pin7, pin10, pin9
  _74161 u_74161_2 (
    .pin1(n74138_1_pin11), .pin2(n7408_1_pin1), .pin7(n74161_2_pin7), .pin14(n74138_1_pin1),
    .pin13(n74138_1_pin2), .pin10(n74161_2_pin10), .pin9(n74161_2_pin9));  // open: pin3, pin4, pin5, pin6, pin15, pin12, pin11
  Clock clock_1 (.out(n7408_1_pin1));
  // also tied to GND on the sheet: {n74161_1_pin3[1], n74161_1_pin3[3], n74161_1_pin9, n74161_1_pin7, n74161_1_pin10, n74138_1_pin4, n74138_1_pin5}
  // also tied to VCC on the sheet: {n74161_1_pin3[0], n74161_1_pin3[2], n74161_1_pin1, n74138_1_pin6, n74161_2_pin10, n74161_2_pin7, n74161_2_pin9}
endmodule
