// Logisim project circuit.circ as structural Verilog
module RegisterUnit4 (
  input  CNT,
  input  LD,
  input  EC,
  input  [3:0] D,
  input  R,
  output [3:0] Q,
  output CA
);

  wire n74161_1_pin1, n74161_1_pin2, n74161_1_pin9;

  _74161 u_74161_1 (
    .pin1(n74161_1_pin1), .pin2(n74161_1_pin2), .pin3(D[0]), .pin4(D[1]), .pin5(D[2]), .pin6(D[3]),
    .pin7(EC), .pin15(CA), .pin14(Q[0]), .pin13(Q[1]), .pin12(Q[2]), .pin11(Q[3]), .pin10(CNT),
    .pin9(n74161_1_pin9));
  not not_1 (n74161_1_pin1, R);
  not not_2 (n74161_1_pin9, LD);
  Clock CP (.out(n74161_1_pin2));
endmodule

module DataRegister (
  input  [7:0] D,
  input  LD,
  input  CNT,
  input  R,
  output [7:0] Q,
  output Z
);

  wire or_1_out, or_2_out, or_3_out, or_4_out, or_5_out, or_6_out, or_7_out, registerunit4_1_ca;

  not not_1 (Z, or_2_out);
  or or_1 (or_1_out, or_4_out, or_5_out);
  or or_2 (or_2_out, or_1_out, or_3_out);
  or or_3 (or_3_out, or_6_out, or_7_out);
  or or_4 (or_4_out, Q[7], Q[6]);
  or or_5 (or_5_out, Q[5], Q[4]);
  or or_6 (or_6_out, Q[3], Q[2]);
  or or_7 (or_7_out, Q[1], Q[0]);
  RegisterUnit4 registerunit4_1 (.CNT(CNT), .LD(LD), .EC(CNT), .D(D[3:0]), .R(R), .Q(Q[3:0]), .CA(registerunit4_1_ca));
  RegisterUnit4 registerunit4_2 (
    .CNT(CNT), .LD(LD), .EC(registerunit4_1_ca), .D(D[7:4]), .R(R), .Q(Q[7:4]));  // open: CA
endmodule

module InstructionRegister (
  input  [7:0] D,
  input  LD,
  input  CNT,
  input  R,
  output V,
  output A,
  output L,
  output Z,
  output [3:0] ICODE
);

  wire registerunit4_1_ca;

  RegisterUnit4 registerunit4_1 (.CNT(CNT), .LD(LD), .EC(CNT), .D(D[3:0]), .R(R), .Q(ICODE), .CA(registerunit4_1_ca));
  RegisterUnit4 registerunit4_2 (
    .CNT(CNT), .LD(LD), .EC(registerunit4_1_ca), .D(D[7:4]), .R(R), .Q({V, A, L, Z}));  // open: CA
endmodule

module InstructionPointerRegister (
);

  RegisterUnit4 registerunit4_1 ();  // open: CNT, LD, EC, D, R, Q, CA
  RegisterUnit4 registerunit4_2 ();  // open: CNT, LD, EC, D, R, Q, CA
  RegisterUnit4 registerunit4_3 ();  // open: CNT, LD, EC, D, R, Q, CA
  RegisterUnit4 registerunit4_4 ();  // open: CNT, LD, EC, D, R, Q, CA
endmodule
