// Logisim project hardware.circ as structural Verilog
module Register4 (
  input  [3:0] D,
  input  BIN,
  input  R,
  input  LD,
  input  CIN,
  input  DEC,
  input  CE,
  output [3:0] Q,
  output B,
  output C
);

  wire clk_out, demultiplexer_1_out0, demultiplexer_1_out1, demultiplexer_2_out0, demultiplexer_2_out1,
       or_1_out, or_2_out, or_3_out, or_4_out;

  Clock clk (.out(clk_out));
  Demultiplexer demultiplexer_1 (.out0(demultiplexer_1_out0), .out1(demultiplexer_1_out1), .in(clk_out), .sel(DEC));
  Demultiplexer demultiplexer_2 (.out0(demultiplexer_2_out0), .out1(demultiplexer_2_out1), .in(CE), .sel(DEC));
  or or_1 (or_1_out, demultiplexer_1_out0, demultiplexer_2_out1);
  or or_2 (or_2_out, demultiplexer_1_out1, demultiplexer_2_out0);
  or or_3 (or_3_out, BIN, or_2_out);
  or or_4 (or_4_out, or_1_out, CIN);
  _74193 u_74193_1 (
    .pin1(D[1]), .pin2(Q[1]), .pin3(Q[0]), .pin4(or_3_out), .pin5(or_4_out), .pin6(Q[2]), .pin7(Q[3]),
    .pin15(D[0]), .pin14(R), .pin13(B), .pin12(C), .pin11(LD), .pin10(D[2]), .pin9(D[3]));
endmodule

module DataRegister (
  input  [7:0] D,
  input  DEC,
  input  CE,
  input  LD,
  input  R,
  output [7:0] Q
);

  wire register4_1_c;

  Register4 register4_1 (
    .D(D[3:0]), .R(R), .LD(LD), .DEC(DEC), .CE(CE), .Q(Q[3:0]), .C(register4_1_c));  // open: BIN, CIN, B
  Register4 register4_2 (.D(D[7:4]), .R(R), .LD(LD), .CIN(register4_1_c), .CE(CE), .Q(Q[7:4]));  // open: BIN, DEC, B, C
endmodule
