// Logisim project bfcpu.circ as structural Verilog: 10 circuits, main circuit Register4
module main (
  input  in_1,
  input  in_2
);

  wire A_OUT, CLK, CLR_DP, CLR_K, D_CLK, D_D, D_DP, D_IP, D_LS, D_SP, DEC, EN_D, EN_IN, EN_IP, EN_OUT, EN_SP,
       HLT, INC, K_OUT, LD_D, LD_FA, LD_FBI, LD_IP, M_CLK, not_1_out, OE_RAM, or_1_out, register4_1_z,
       register4_2_z, register4_3_z, register8_2_z, register16_1_z, register16_2_z, S_OUT, U_D, U_DP, U_IP,
       U_LS, U_SP, V_OUT, WE_RAM, Z_OUT;
  wire [2:0] RS;
  wire [3:0] I_OUT, programrom_1_cmd, register4_2_d_out, VASZ;
  wire [7:0] register8_3_d_out;
  wire [15:0] ADDRESS_BUS, D_OUT;

  Clock clock_1 (.out(CLK));
  or or_1 (or_1_out, CLR_DP, in_1);
  ClockModule clockmodule_1 (.CLR(in_1), .CLK(CLK), .HLT(HLT), .RESUME(in_2), .D_CLK(D_CLK), .M_CLK(M_CLK));
  not not_1 (not_1_out, EN_SP);
  Register8 register8_1 (
    .RESET(in_1), .CLK(M_CLK), .EN(EN_D), .LD(LD_D), .DN(U_D), .UP(D_D), .D_IN(D_OUT[7:0]), .Z(Z_OUT),
    .D_OUT(D_OUT[7:0]));
  // NoConnect on register8_2_z
  Register8 register8_2 (
    .RESET(in_1), .CLK(M_CLK), .EN(EN_SP), .LD(1'b0), .DN(U_SP), .UP(D_SP), .D_IN({8{1'b0}}),
    .Z(register8_2_z), .D_OUT(ADDRESS_BUS[7:0]));
  // NoConnect on register16_1_z
  Register16 register16_1 (
    .D_IN(D_OUT), .RESET(in_1), .CLK(M_CLK), .EN(EN_IP), .LD(LD_IP), .DN(U_IP), .UP(D_IP),
    .Z(register16_1_z), .D_OUT(D_OUT));
  assign D_OUT[15:8] = EN_D ? {8{1'b0}} : 8'bz;  // Controlled_Buffer controlled_buffer_1
  assign ADDRESS_BUS[15:8] = EN_SP ? {8{1'b0}} : 8'bz;  // Controlled_Buffer controlled_buffer_2
  // NoConnect on register16_2_z
  Register16 register16_2 (
    .D_IN(16'h100), .CLK(M_CLK), .EN(not_1_out), .LD(or_1_out), .DN(U_DP), .UP(D_DP), .Z(register16_2_z),
    .D_OUT(ADDRESS_BUS));  // open: RESET
  RegisterDriver registerdriver_1 (
    .RS(RS), .INC(INC), .DEC(DEC), .M_CLK(CLK), .U_D(U_D), .U_DP(U_DP), .U_SP(U_SP), .U_IP(U_IP),
    .U_LS(U_LS), .D_D(D_D), .D_DP(D_DP), .D_SP(D_SP), .D_IP(D_IP), .D_LS(D_LS));
  Register8 register8_3 (
    .RESET(in_1), .CLK(M_CLK), .EN(1'b0), .LD(1'b0), .DN(U_LS), .UP(D_LS), .D_IN({8{1'b0}}), .Z(S_OUT),
    .D_OUT(register8_3_d_out));
  // NoConnect on register8_3_d_out
  RamModule rammodule_1 (
    .ADDR_IN(ADDRESS_BUS), .WE(WE_RAM), .OE(OE_RAM), .CLK(M_CLK), .DATA_IN(D_OUT), .DATA_OUT(D_OUT));
  ProgramROM programrom_1 (.ADDR(D_OUT), .CMD(programrom_1_cmd));
  // NoConnect on register4_1_z
  Register4 register4_1 (
    .EN(1'b1), .LD(LD_FBI), .DN(1'b0), .UP(1'b0), .CLK(M_CLK), .D_IN(programrom_1_cmd), .RESET(in_1),
    .Z(register4_1_z), .D_OUT(I_OUT));
  // NoConnect on register4_2_z
  Register4 register4_2 (
    .EN(1'b1), .LD(LD_FA), .DN(1'b0), .UP(1'b0), .CLK(M_CLK), .D_IN({V_OUT, A_OUT, 2'b00}), .RESET(in_1),
    .Z(register4_2_z), .D_OUT(register4_2_d_out));
  ControlUnit controlunit_1 (
    .CLR(in_1), .CLK(D_CLK), .KVASZ({K_OUT, VASZ}), .CMD(I_OUT), .INC(INC), .DEC(DEC), .CLR_DP(CLR_DP),
    .EN_SP(EN_SP), .OE_RAM(OE_RAM), .WE_RAM(WE_RAM), .EN_IN(EN_IN), .EN_OUT(EN_OUT), .V_OUT(V_OUT),
    .A_OUT(A_OUT), .LD_FBI(LD_FBI), .LD_FA(LD_FA), .EN_IP(EN_IP), .LD_IP(LD_IP), .EN_D(EN_D), .LD_D(LD_D),
    .CLR_K(CLR_K), .HLT(HLT), .RS(RS));
  // NoConnect on register4_3_z
  Register4 register4_3 (
    .EN(1'b0), .LD(LD_FBI), .DN(1'b0), .UP(1'b0), .CLK(M_CLK), .D_IN({register4_2_d_out[3:2], S_OUT, Z_OUT}),
    .RESET(in_1), .Z(register4_3_z), .D_OUT(VASZ));
  IOModule iomodule_1 (.CLR_K(CLR_K), .DATA_IN(D_OUT[7:0]), .CLK(M_CLK), .EN_OUT(EN_OUT), .CLR(in_1), .K_OUT(K_OUT));

  // Other names for the same wires on the sheet: CLR = in_1; DATA_BUS[15:0] = D_OUT; DATA_BUS_LOW[7:0] = D_OUT[7:0];
  //   IP_OUT[15:0] = D_OUT; DATA_BUS_HIGH[7:0] = D_OUT[15:8]; RESUME = in_2; DP_OUT[15:0] = ADDRESS_BUS;
  //   SP_OUT[15:0] = ADDRESS_BUS
endmodule

module Register4 (
  input  CLK,
  input  EN,
  input  LD,
  input  DN,
  input  UP,
  input  [3:0] D_IN,
  input  RESET,
  output [3:0] D_OUT,
  output Z
);

  wire n74193_1_pin11;
  wire [3:0] n74193_1_pin3;

  _74193 u_74193_1 (
    .pin1(D_IN[1]), .pin2(n74193_1_pin3[1]), .pin3(n74193_1_pin3[0]), .pin4(DN), .pin5(UP),
    .pin6(n74193_1_pin3[2]), .pin7(n74193_1_pin3[3]), .pin15(D_IN[0]), .pin14(RESET), .pin11(n74193_1_pin11),
    .pin10(D_IN[2]), .pin9(D_IN[3]));  // open: pin13, pin12
  nand nand_1 (n74193_1_pin11, LD, CLK);
  Hex_Digit_Display hex_digit_display_1 (.value(n74193_1_pin3));  // open: dp
  nor nor_1 (Z, n74193_1_pin3[3], n74193_1_pin3[2], n74193_1_pin3[1], n74193_1_pin3[0]);
  assign D_OUT = EN ? n74193_1_pin3 : 4'bz;  // Controlled_Buffer controlled_buffer_1
endmodule

module Register8 (
  input  [7:0] D_IN,
  input  CLK,
  input  EN,
  input  LD,
  input  DN,
  input  UP,
  input  RESET,
  output [7:0] D_OUT,
  output Z
);

  wire n74193_1_pin12, n74193_1_pin13, nand_1_out, or_1_out, or_2_out;
  wire [3:0] n74193_1_pin3, n74193_2_pin3;

  nand nand_1 (nand_1_out, CLK, LD);
  _74193 u_74193_1 (
    .pin1(D_IN[1]), .pin2(n74193_1_pin3[1]), .pin3(n74193_1_pin3[0]), .pin4(DN), .pin5(UP),
    .pin6(n74193_1_pin3[2]), .pin7(n74193_1_pin3[3]), .pin15(D_IN[0]), .pin14(RESET), .pin13(n74193_1_pin13),
    .pin12(n74193_1_pin12), .pin11(nand_1_out), .pin10(D_IN[2]), .pin9(D_IN[3]));
  Hex_Digit_Display hex_digit_display_1 (.value(n74193_1_pin3));  // open: dp
  or or_1 (or_1_out, n74193_1_pin3[3], n74193_1_pin3[2], n74193_1_pin3[1], n74193_1_pin3[0]);
  assign D_OUT[7:4] = EN ? n74193_1_pin3 : 4'bz;  // Controlled_Buffer controlled_buffer_1
  _74193 u_74193_2 (
    .pin1(D_IN[5]), .pin2(n74193_2_pin3[1]), .pin3(n74193_2_pin3[0]), .pin4(n74193_1_pin13),
    .pin5(n74193_1_pin12), .pin6(n74193_2_pin3[2]), .pin7(n74193_2_pin3[3]), .pin15(D_IN[4]), .pin14(RESET),
    .pin11(nand_1_out), .pin10(D_IN[6]), .pin9(D_IN[7]));  // open: pin13, pin12
  Hex_Digit_Display hex_digit_display_2 (.value(n74193_2_pin3));  // open: dp
  or or_2 (or_2_out, n74193_2_pin3[3], n74193_2_pin3[2], n74193_2_pin3[1], n74193_2_pin3[0]);
  assign D_OUT[3:0] = EN ? n74193_2_pin3 : 4'bz;  // Controlled_Buffer controlled_buffer_2
  nor nor_1 (Z, or_2_out, or_1_out);

  // Other names for the same wires on the sheet: R = RESET
endmodule

module Register16 (
  input  [15:0] D_IN,
  input  CLK,
  input  EN,
  input  LD,
  input  DN,
  input  UP,
  input  RESET,
  output [15:0] D_OUT,
  output Z
);

  wire n74193_1_pin12, n74193_1_pin13, n74193_2_pin12, n74193_2_pin13, n74193_3_pin12, n74193_3_pin13,
       nand_1_out, or_1_out, or_2_out, or_3_out, or_4_out;
  wire [3:0] n74193_1_pin3, n74193_2_pin3, n74193_3_pin3, n74193_4_pin3;

  nand nand_1 (nand_1_out, CLK, LD);
  _74193 u_74193_1 (
    .pin1(D_IN[1]), .pin2(n74193_1_pin3[1]), .pin3(n74193_1_pin3[0]), .pin4(DN), .pin5(UP),
    .pin6(n74193_1_pin3[2]), .pin7(n74193_1_pin3[3]), .pin15(D_IN[0]), .pin14(RESET), .pin13(n74193_1_pin13),
    .pin12(n74193_1_pin12), .pin11(nand_1_out), .pin10(D_IN[2]), .pin9(D_IN[3]));
  or or_1 (or_1_out, n74193_1_pin3[3], n74193_1_pin3[2], n74193_1_pin3[1], n74193_1_pin3[0]);
  Hex_Digit_Display hex_digit_display_1 (.value(n74193_1_pin3));  // open: dp
  assign D_OUT[3:0] = EN ? n74193_1_pin3 : 4'bz;  // Controlled_Buffer controlled_buffer_1
  _74193 u_74193_2 (
    .pin1(D_IN[5]), .pin2(n74193_2_pin3[1]), .pin3(n74193_2_pin3[0]), .pin4(n74193_1_pin13),
    .pin5(n74193_1_pin12), .pin6(n74193_2_pin3[2]), .pin7(n74193_2_pin3[3]), .pin15(D_IN[4]), .pin14(RESET),
    .pin13(n74193_2_pin13), .pin12(n74193_2_pin12), .pin11(nand_1_out), .pin10(D_IN[6]), .pin9(D_IN[7]));
  Hex_Digit_Display hex_digit_display_2 (.value(n74193_2_pin3));  // open: dp
  or or_2 (or_2_out, n74193_2_pin3[3], n74193_2_pin3[2], n74193_2_pin3[1], n74193_2_pin3[0]);
  assign D_OUT[7:4] = EN ? n74193_2_pin3 : 4'bz;  // Controlled_Buffer controlled_buffer_2
  _74193 u_74193_3 (
    .pin1(D_IN[9]), .pin2(n74193_3_pin3[1]), .pin3(n74193_3_pin3[0]), .pin4(n74193_2_pin13),
    .pin5(n74193_2_pin12), .pin6(n74193_3_pin3[2]), .pin7(n74193_3_pin3[3]), .pin15(D_IN[8]), .pin14(RESET),
    .pin13(n74193_3_pin13), .pin12(n74193_3_pin12), .pin11(nand_1_out), .pin10(D_IN[10]), .pin9(D_IN[11]));
  Hex_Digit_Display hex_digit_display_3 (.value(n74193_3_pin3));  // open: dp
  or or_3 (or_3_out, n74193_3_pin3[3], n74193_3_pin3[2], n74193_3_pin3[1], n74193_3_pin3[0]);
  assign D_OUT[11:8] = EN ? n74193_3_pin3 : 4'bz;  // Controlled_Buffer controlled_buffer_3
  _74193 u_74193_4 (
    .pin1(D_IN[13]), .pin2(n74193_4_pin3[1]), .pin3(n74193_4_pin3[0]), .pin4(n74193_3_pin13),
    .pin5(n74193_3_pin12), .pin6(n74193_4_pin3[2]), .pin7(n74193_4_pin3[3]), .pin15(D_IN[12]), .pin14(RESET),
    .pin11(nand_1_out), .pin10(D_IN[14]), .pin9(D_IN[15]));  // open: pin13, pin12
  Hex_Digit_Display hex_digit_display_4 (.value(n74193_4_pin3));  // open: dp
  or or_4 (or_4_out, n74193_4_pin3[3], n74193_4_pin3[2], n74193_4_pin3[1], n74193_4_pin3[0]);
  assign D_OUT[15:12] = EN ? n74193_4_pin3 : 4'bz;  // Controlled_Buffer controlled_buffer_4
  nor nor_1 (Z, or_4_out, or_3_out, or_2_out, or_1_out);

  // Other names for the same wires on the sheet: R = RESET
endmodule

module RegisterDriver (
  input  [2:0] RS,
  input  INC,
  input  DEC,
  input  M_CLK,
  output U_D,
  output U_DP,
  output U_SP,
  output U_IP,
  output U_LS,
  output D_D,
  output D_DP,
  output D_SP,
  output D_IP,
  output D_LS
);

  wire not_1_out, not_2_out;

  not not_1 (not_1_out, INC);
  not not_2 (not_2_out, DEC);
  _74138 u_74138_1 (
    .pin1(RS[0]), .pin2(RS[1]), .pin3(RS[2]), .pin4(not_1_out), .pin5(not_1_out), .pin6(M_CLK), .pin14(U_D),
    .pin13(U_DP), .pin12(U_SP), .pin11(U_IP), .pin10(U_LS));  // open: pin7, pin15, pin9
  _74138 u_74138_2 (
    .pin1(RS[0]), .pin2(RS[1]), .pin3(RS[2]), .pin4(not_2_out), .pin5(not_2_out), .pin6(M_CLK), .pin14(D_D),
    .pin13(D_DP), .pin12(D_SP), .pin11(D_IP), .pin10(D_LS));  // open: pin7, pin15, pin9
endmodule

module ControlUnit (
  input  [4:0] KVASZ,
  input  [3:0] CMD,
  input  CLR,
  input  CLK,
  output HLT,
  output [2:0] RS,
  output INC,
  output DEC,
  output CLR_DP,
  output EN_SP,
  output OE_RAM,
  output WE_RAM,
  output EN_IN,
  output EN_OUT,
  output V_OUT,
  output A_OUT,
  output LD_FBI,
  output LD_FA,
  output EN_IP,
  output LD_IP,
  output EN_D,
  output LD_D,
  output CLR_K
);

  wire CR, n74161_1_pin7, nor_1_out, not_1_out;
  wire [2:0] n74161_1_pin14;
  wire [3:3] n74161_1_pin11;
  wire [7:0] ROM1_data, ROM2_data, ROM3_data;
  wire [7:6] register_3_q;
  wire [24:0] multiplexer_1_out;

  nor nor_1 (nor_1_out, CLR, CR);
  Multiplexer #(.select(4), .width(25)) multiplexer_1 (
    .in0(25'h1f4105f), .in1(25'h427c84), .in2(25'h421084), .in3(25'h454400), .in4(25'h4544), .in5(25'h35c0),
    .in6(25'h18c0), .in7(25'hfc400), .in8(25'h47e0), .out(multiplexer_1_out), .sel(CMD));  // open: in9, in10, in11, in12, in13, in14, in15
  ROM #(.addrWidth(13)) ROM1 (.addr({1'b0, KVASZ, CMD, n74161_1_pin14}), .data(ROM1_data));
  Hex_Digit_Display hex_digit_display_1 (.value(CMD));  // open: dp
  _74161 u_74161_1 (
    .pin1(nor_1_out), .pin2(CLK), .pin7(n74161_1_pin7), .pin14(n74161_1_pin14[0]), .pin13(n74161_1_pin14[1]),
    .pin12(n74161_1_pin14[2]), .pin11(n74161_1_pin11[3]), .pin10(n74161_1_pin7));  // open: pin3, pin4, pin5, pin6, pin15, pin9
  DotMatrix #(.matrixrows(5)) dotmatrix_1 (
    .col0(multiplexer_1_out[24:20]), .col1(multiplexer_1_out[19:15]), .col2(multiplexer_1_out[14:10]),
    .col3(multiplexer_1_out[9:5]), .col4(multiplexer_1_out[4:0]));
  ROM #(.addrWidth(13)) ROM2 (.addr({1'b0, KVASZ, CMD, n74161_1_pin14}), .data(ROM2_data));
  Hex_Digit_Display hex_digit_display_2 (.value({n74161_1_pin11[3], n74161_1_pin14}));  // open: dp
  ROM #(.addrWidth(13)) ROM3 (.addr({1'b0, KVASZ, CMD, n74161_1_pin14}), .data(ROM3_data));
  Register register_1 (.D(ROM1_data), .en(1'b1), .clk(CLK), .Q({EN_SP, CLR_DP, DEC, INC, RS, HLT}), .clr(CLR));
  Register register_2 (
    .D(ROM2_data), .en(1'b1), .clk(CLK), .Q({LD_FA, LD_FBI, A_OUT, V_OUT, EN_OUT, EN_IN, WE_RAM, OE_RAM}),
    .clr(CLR));
  Register register_3 (
    .D(ROM3_data), .en(1'b1), .clk(CLK), .Q({register_3_q, CLR_K, CR, LD_D, EN_D, LD_IP, EN_IP}), .clr(CLR));
  // NoConnect on register_3_q[7]
  not not_1 (not_1_out, register_3_q[6]);
  LED led_1 (.in(not_1_out));
  LED led_2 (.in(register_3_q[6]));
  // also tied to VCC on the sheet: n74161_1_pin7

  // Other names for the same wires on the sheet: I[3:0] = CMD

  // Notes on the sheet:
  //   contents of ROM1 (hex, n*v repeats v):
  //   0 18 6*1 0 12 18 5*1 0 22 18 5*1 0 24 18 5*1 0 14 18 5*1 0 0 0 5*1 0 0 0 5*1 0 16 80 18 4*1 0 80 18
  //   5*1 0 0 0 21*1 0 0 6*1 0 7*1 0 58 6*1 0 1 18 5*1 0 18 6*1 0 12 18 5*1 0 22 18 5*1 0 24 18 5*1 0 14
  //   18 5*1 0 0 0 5*1 0 0 0 5*1 0 1a 18 5*1 0 26 18 5*1 0 0 0 21*1 0 0 6*1 0 1a 14 18 4*1 0 58 6*1 0 1 18
  //   5*1 0 18 6*1 0 18 6*1 0 18 6*1 0 18 6*1 0 18 6*1 0 18 6*1 0 18 6*1 0 1a 18 5*1 0 2a 18 5*1 0 18 22*1
  //   0 0 6*1 0 7*1 0 58 6*1 0 1 18 5*1 0 18 6*1 0 18 6*1 0 18 6*1 0 18 6*1 0 18 6*1 0 18 6*1 0 18 6*1 0
  //   1a 18 5*1 0 2a 18 5*1 0 18 22*1 0 0 6*1 0 1a 14 0 4*1 0 58 6*1 0 1 18 5*1 0 18 6*1 0 0 12 18 4*1 0 0
  //   22 18 4*1 0 24 18 5*1 0 14 18 5*1 0 0 0 5*1 0 0 0 5*1 0 0 6*1 0 0 6*1 0 0 0 21*1 0 0 6*1 0 7*1 0 58
  //   6*1 0 1 18 5*1 0 18 6*1 0 0 12 18 4*1 0 0 22 18 4*1 0 24 18 5*1 0 14 18 5*1 0 0 0 5*1 0 0 0 5*1 0 0
  //   6*1 0 0 6*1 0 0 0 21*1 0 0 6*1 0 1a 14 18 4*1 0 58 6*1 0 1 18 5*1 0 18 6*1 0 18 6*1 0 18 6*1 0 18
  //   6*1 0 18 6*1 0 18 6*1 0 18 6*1 0 1a 18 5*1 0 2a 18 5*1 0 18 22*1 0 0 6*1 0 7*1 0 58 6*1 0 1 18 5*1 0
  //   18 6*1 0 18 6*1 0 18 6*1 0 18 6*1 0 18 6*1 0 18 6*1 0 18 6*1 0 1a 18 5*1 0 2a 18 5*1 0 18 22*1 0 0
  //   6*1 0 1a 14 0 4*1 0 58 6*1 0 1 18 5*1 0 18 6*1 0 12 18 5*1 0 22 18 5*1 0 0 24 18 4*1 0 0 14 18 4*1 0
  //   0 0 5*1 0 0 0 5*1 0 16 80 18 4*1 0 80 18 5*1 0 0 0 21*1 0 0 6*1 0 7*1 0 58 6*1 0 1 18 5*1 0 18 6*1 0
  //   12 18 5*1 0 22 18 5*1 0 0 24 18 4*1 0 0 14 18 4*1 0 0 0 5*1 0 0 0 5*1 0 1a 18 5*1 0 26 18 5*1 0 0 0
  //   21*1 0 0 6*1 0 1a 14 18 4*1 0 58 6*1 0 1 18 5*1 0 18 6*1 0 18 6*1 0 18 6*1 0 18 6*1 0 18 6*1 0 18
  //   6*1 0 18 6*1 0 1a 18 5*1 0 2a 18 5*1 0 18 22*1 0 0 6*1 0 7*1 0 58 6*1 0 1 18 5*1 0 18 6*1 0 18 6*1 0
  //   18 6*1 0 18 6*1 0 18 6*1 0 18 6*1 0 18 6*1 0 1a 18 5*1 0 2a 18 5*1 0 18 22*1 0 0 6*1 0 1a 14 0 4*1 0
  //   58 6*1 0 1 18 5*1 0 18 6*1 0 0 12 18 4*1 0 0 22 18 4*1 0 0 24 18 4*1 0 0 14 18 4*1 0 0 0 5*1 0 0 0
  //   5*1 0 0 6*1 0 0 6*1 0 0 0 21*1 0 0 6*1 0 7*1 0 58 6*1 0 1 18 5*1 0 18 6*1 0 0 12 18 4*1 0 0 22 18
  //   4*1 0 0 24 18 4*1 0 0 14 18 4*1 0 0 0 5*1 0 0 0 5*1 0 0 6*1 0 0 6*1 0 0 0 21*1 0 0 6*1 0 1a 14 18
  //   4*1 0 58 6*1 0 1 18 5*1 0 18 6*1 0 18 6*1 0 18 6*1 0 18 6*1 0 18 6*1 0 18 6*1 0 18 6*1 0 1a 18 5*1 0
  //   2a 18 5*1 0 18 22*1 0 0 6*1 0 7*1 0 58 6*1 0 1 18 5*1 0 18 6*1 0 18 6*1 0 18 6*1 0 18 6*1 0 18 6*1 0
  //   18 6*1 0 18 6*1 0 1a 18 5*1 0 2a 18 5*1 0 18 22*1 0 0 6*1 0 1a 14 0 4*1 0 58 6*1 0 1 18 5*1 0 18 6*1
  //   0 12 18 5*1 0 22 18 5*1 0 24 18 5*1 0 14 18 5*1 0 0 0 18 4*1 0 0 18 5*1 0 16 80 18 4*1 0 80 18 5*1 0
  //   0 18 21*1 0 18 6*1 0 7*1 0 58 6*1 0 1 18 5*1 0 18 6*1 0 12 18 5*1 0 22 18 5*1 0 24 18 5*1 0 14 18
  //   5*1 0 0 0 18 4*1 0 0 18 5*1 0 1a 18 5*1 0 26 18 5*1 0 0 18 21*1 0 18 6*1 0 1a 14 18 4*1 0 58 6*1 0 1
  //   18 5*1 0 18 6*1 0 18 6*1 0 18 6*1 0 18 6*1 0 18 6*1 0 18 6*1 0 18 6*1 0 1a 18 5*1 0 2a 18 5*1 0 18
  //   22*1 0 18 6*1 0 7*1 0 58 6*1 0 1 18 5*1 0 18 6*1 0 18 6*1 0 18 6*1 0 18 6*1 0 18 6*1 0 18 6*1 0 18
  //   6*1 0 1a 18 5*1 0 2a 18 5*1 0 18 22*1 0 18 6*1 0 1a 14 0 4*1 0 58 6*1 0 1 18 5*1 0 18 6*1 0 0 12 18
  //   4*1 0 0 22 18 4*1 0 24 18 5*1 0 14 18 5*1 0 0 0 18 4*1 0 0 18 5*1 0 0 6*1 0 0 6*1 0 0 18 21*1 0 18
  //   6*1 0 7*1 0 58 6*1 0 1 18 5*1 0 18 6*1 0 0 12 18 4*1 0 0 22 18 4*1 0 24 18 5*1 0 14 18 5*1 0 0 0 18
  //   4*1 0 0 18 5*1 0 0 6*1 0 0 6*1 0 0 18 21*1 0 18 6*1 0 1a 14 18 4*1 0 58 6*1 0 1 18 5*1 0 18 6*1 0 18
  //   6*1 0 18 6*1 0 18 6*1 0 18 6*1 0 18 6*1 0 18 6*1 0 1a 18 5*1 0 2a 18 5*1 0 18 22*1 0 18 6*1 0 7*1 0
  //   58 6*1 0 1 18 5*1 0 18 6*1 0 18 6*1 0 18 6*1 0 18 6*1 0 18 6*1 0 18 6*1 0 18 6*1 0 1a 18 5*1 0 2a 18
  //   5*1 0 18 22*1 0 18 6*1 0 1a 14 0 4*1 0 58 6*1 0 1 18 5*1 0 18 6*1 0 12 18 5*1 0 22 18 5*1 0 0 24 18
  //   4*1 0 0 14 18 4*1 0 0 0 18 4*1 0 0 18 5*1 0 16 80 18 4*1 0 80 18 5*1 0 0 18 21*1 0 18 6*1 0 7*1 0 58
  //   6*1 0 1 18 5*1 0 18 6*1 0 12 18 5*1 0 22 18 5*1 0 0 24 18 4*1 0 0 14 18 4*1 0 0 0 18 4*1 0 0 18 5*1
  //   0 1a 18 5*1 0 26 18 5*1 0 0 18 21*1 0 18 6*1 0 1a 14 18 4*1 0 58 6*1 0 1 18 5*1 0 18 6*1 0 18 6*1 0
  //   18 6*1 0 18 6*1 0 18 6*1 0 18 6*1 0 18 6*1 0 1a 18 5*1 0 2a 18 5*1 0 18 22*1 0 18 6*1 0 7*1 0 58 6*1
  //   0 1 18 5*1 0 18 6*1 0 18 6*1 0 18 6*1 0 18 6*1 0 18 6*1 0 18 6*1 0 18 6*1 0 1a 18 5*1 0 2a 18 5*1 0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
  //   Cycle Count
  //   contents of ROM2 (hex, n*v repeats v):
  //   40 7*0 40 90 6*0 40 90 6*0 40 a0 6*0 40 a0 6*0 40 4 6*0 40 8 6*0 40 0 2 5*0 40 1 6*0 40 c 22*0 40
  //   7*0 40 7*0 40 7*0 40 7*0 40 7*0 40 90 6*0 40 90 6*0 40 a0 6*0 40 a0 6*0 40 4 6*0 40 8 6*0 40 7*0 40
  //   7*0 40 c 22*0 40 7*0 40 2 40 5*0 40 7*0 40 7*0 40 7*0 40 7*0 40 7*0 40 7*0 40 7*0 40 7*0 40 7*0 40
  //   7*0 40 7*0 40 23*0 40 7*0 40 7*0 40 7*0 40 7*0 40 7*0 40 7*0 40 7*0 40 7*0 40 7*0 40 7*0 40 7*0 40
  //   7*0 40 7*0 40 23*0 40 7*0 40 2 40 5*0 40 7*0 40 7*0 40 7*0 40 1 90 5*0 40 1 90 5*0 40 a0 6*0 40 a0
  //   6*0 40 4 6*0 41 9 1 5*0 40 81 6*0 40 81 6*0 40 c 22*0 40 7*0 40 7*0 40 7*0 40 7*0 40 7*0 40 1 90 5*0
  //   40 1 90 5*0 40 a0 6*0 40 a0 6*0 40 4 6*0 41 9 1 5*0 40 81 6*0 40 81 6*0 40 c 22*0 40 7*0 40 2 40 5*0
  //   40 7*0 40 7*0 40 7*0 40 7*0 40 7*0 40 7*0 40 7*0 40 7*0 41 7*0 40 7*0 40 7*0 40 23*0 40 7*0 40 7*0
  //   40 7*0 40 7*0 40 7*0 40 7*0 40 7*0 40 7*0 40 7*0 40 7*0 41 7*0 40 7*0 40 7*0 40 23*0 40 7*0 40 2 40
  //   5*0 40 7*0 40 7*0 40 7*0 40 90 6*0 40 90 6*0 40 2 a0 5*0 40 2 a0 5*0 40 4 6*0 40 8 6*0 40 0 2 5*0 40
  //   1 6*0 40 c 22*0 40 7*0 40 7*0 40 7*0 40 7*0 40 7*0 40 90 6*0 40 90 6*0 40 2 a0 5*0 40 2 a0 5*0 40 4
  //   6*0 40 8 6*0 40 7*0 40 7*0 40 c 22*0 40 7*0 40 2 40 5*0 40 7*0 40 7*0 40 7*0 40 7*0 40 7*0 40 7*0 40
  //   7*0 40 7*0 40 7*0 40 7*0 40 7*0 40 23*0 40 7*0 40 7*0 40 7*0 40 7*0 40 7*0 40 7*0 40 7*0 40 7*0 40
  //   7*0 40 7*0 40 7*0 40 7*0 40 7*0 40 23*0 40 7*0 40 2 40 5*0 40 7*0 40 7*0 40 7*0 40 1 90 5*0 40 1 90
  //   5*0 40 2 a0 5*0 40 2 a0 5*0 40 4 6*0 41 9 1 5*0 40 81 6*0 40 81 6*0 40 c 22*0 40 7*0 40 7*0 40 7*0
  //   40 7*0 40 7*0 40 1 90 5*0 40 1 90 5*0 40 2 a0 5*0 40 2 a0 5*0 40 4 6*0 41 9 1 5*0 40 81 6*0 40 81
  //   6*0 40 c 22*0 40 7*0 40 2 40 5*0 40 7*0 40 7*0 40 7*0 40 7*0 40 7*0 40 7*0 40 7*0 40 7*0 41 7*0 40
  //   7*0 40 7*0 40 23*0 40 7*0 40 7*0 40 7*0 40 7*0 40 7*0 40 7*0 40 7*0 40 7*0 40 7*0 40 7*0 41 7*0 40
  //   7*0 40 7*0 40 23*0 40 7*0 40 2 40 5*0 40 7*0 40 7*0 40 7*0 40 90 6*0 40 90 6*0 40 a0 6*0 40 a0 6*0
  //   40 4 90 5*0 40 8 6*0 40 0 2 5*0 40 1 6*0 40 90 22*0 40 7*0 40 7*0 40 7*0 40 7*0 40 7*0 40 90 6*0 40
  //   90 6*0 40 a0 6*0 40 a0 6*0 40 4 90 5*0 40 8 6*0 40 7*0 40 7*0 40 90 22*0 40 7*0 40 2 40 5*0 40 7*0
  //   40 7*0 40 7*0 40 7*0 40 7*0 40 7*0 40 7*0 40 7*0 40 7*0 40 7*0 40 7*0 40 23*0 40 7*0 40 7*0 40 7*0
  //   40 7*0 40 7*0 40 7*0 40 7*0 40 7*0 40 7*0 40 7*0 40 7*0 40 7*0 40 7*0 40 23*0 40 7*0 40 2 40 5*0 40
  //   7*0 40 7*0 40 7*0 40 1 90 5*0 40 1 90 5*0 40 a0 6*0 40 a0 6*0 40 4 90 5*0 41 9 6*0 40 81 6*0 40 81
  //   6*0 40 90 22*0 40 7*0 40 7*0 40 7*0 40 7*0 40 7*0 40 1 90 5*0 40 1 90 5*0 40 a0 6*0 40 a0 6*0 40 4
  //   90 5*0 41 9 6*0 40 81 6*0 40 81 6*0 40 90 22*0 40 7*0 40 2 40 5*0 40 7*0 40 7*0 40 7*0 40 7*0 40 7*0
  //   40 7*0 40 7*0 40 7*0 41 7*0 40 7*0 40 7*0 40 23*0 40 7*0 40 7*0 40 7*0 40 7*0 40 7*0 40 7*0 40 7*0
  //   40 7*0 40 7*0 40 7*0 41 7*0 40 7*0 40 7*0 40 23*0 40 7*0 40 2 40 5*0 40 7*0 40 7*0 40 7*0 40 90 6*0
  //   40 90 6*0 40 2 a0 5*0 40 2 a0 5*0 40 4 90 5*0 40 8 6*0 40 0 2 5*0 40 1 6*0 40 90 22*0 40 7*0 40 7*0
  //   40 7*0 40 7*0 40 7*0 40 90 6*0 40 90 6*0 40 2 a0 5*0 40 2 a0 5*0 40 4 90 5*0 40 8 6*0 40 7*0 40 7*0
  //   40 90 22*0 40 7*0 40 2 40 5*0 40 7*0 40 7*0 40 7*0 40 7*0 40 7*0 40 7*0 40 7*0 40 7*0 40 7*0 40 7*0
  //   40 7*0 40 23*0 40 7*0 40 7*0 40 7*0 40 7*0 40 7*0 40 7*0 40 7*0 40 7*0 40 7*0 40 7*0 40 7*0 40 7*0
  //   40 7*0 40 23*0 40 7*0 40 2 40 5*0 40 7*0 40 7*0 40 7*0 40 1 90 5*0 40 1 90 5*0 40 2 a0 5*0 40 2 a0
  //   5*0 40 4 90 5*0 41 9 6*0 40 81 6*0 40 81 6*0 40 90 22*0 40 7*0 40 7*0 40 7*0 40 7*0 40 7*0 40 1 90
  //   5*0 40 1 90 5*0 40 2 a0 5*0 40 2 a0 5*0 40 4 90 5*0 41 9 6*0 40 81 6*0 40 81 6*0 40 90 22*0 40 7*0
  //   40 2 40 5*0 40 7*0 40 7*0 40 7*0 40 7*0 40 7*0 40 7*0 40 7*0 40 7*0 41 7*0 40 7*0 40 7*0 40 23*0 40
  //   7*0 40 7*0 40 7*0 40 7*0 40 7*0 40 7*0 40 7*0 40 7*0 40 7*0 40 7*0 41 7*0 40 7*0 40 7*0 40 23*0 40
  //   7*0 40 2 40 5*0 40 7*0 40 7*0 40 7*0 40 90 6*0 40 90 6*0 40 a0 6*0 40 a0 6*0 40 4 6*0 40 8 6*0 40 0
  //   2 5*0 40 1 6*0 40 c 22*0 40 7*0 40 7*0 40 7*0 40 7*0 40 7*0 40 90 6*0 40 90 6*0 40 a0 6*0 40 a0 6*0
  //   40 4 6*0 40 8 6*0 40 7*0 40 7*0 40 c 22*0 40 7*0 40 2 40 5*0 40 7*0 40 7*0 40 7*0 40 7*0 40 7*0 40
  //   7*0 40 7*0 40 7*0 4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
  //   contents of ROM3 (hex, n*v repeats v):
  //   0 10 6*80 0 0 10 5*80 0 0 10 5*80 0 0 10 5*80 0 0 10 5*80 0 0 10 5*80 4 4 14 5*80 0 0 1 10 4*80 0 2
  //   10 5*80 0 0 10 21*80 0 10 6*80 0 7*80 0 10 6*80 0 0 10 5*80 0 10 6*80 0 0 10 5*80 0 0 10 5*80 0 0 10
  //   5*80 0 0 10 5*80 0 0 10 5*80 4 4 14 5*80 0 0 10 5*80 0 0 10 5*80 0 0 10 21*80 0 10 6*80 0 4 0 10
  //   4*80 0 10 6*80 0 0 10 5*80 0 10 6*80 0 10 6*80 0 10 6*80 0 10 6*80 0 10 6*80 0 10 6*80 4 10 6*80 0 0
  //   10 5*80 0 0 10 5*80 0 10 22*80 0 10 6*80 0 7*80 0 10 6*80 0 0 10 5*80 0 10 6*80 0 10 6*80 0 10 6*80
  //   0 10 6*80 0 10 6*80 0 10 6*80 4 10 6*80 0 0 10 5*80 0 0 10 5*80 0 10 22*80 0 10 6*80 0 4 0 10 4*80 0
  //   10 6*80 0 0 10 5*80 0 10 6*80 0 8 0 10 4*80 0 8 0 10 4*80 0 0 10 5*80 0 0 10 5*80 0 0 10 5*80 0 0 10
  //   5*80 0 18 6*80 0 18 6*80 0 0 10 21*80 0 10 6*80 0 7*80 0 10 6*80 0 0 10 5*80 0 10 6*80 0 8 0 10 4*80
  //   0 8 0 10 4*80 0 0 10 5*80 0 0 10 5*80 0 0 10 5*80 0 0 10 5*80 0 18 6*80 0 18 6*80 0 0 10 21*80 0 10
  //   6*80 0 4 0 10 4*80 0 10 6*80 0 0 10 5*80 0 10 6*80 0 10 6*80 0 10 6*80 0 10 6*80 0 10 6*80 0 10 6*80
  //   0 10 6*80 0 0 10 5*80 0 0 10 5*80 0 10 22*80 0 10 6*80 0 7*80 0 10 6*80 0 0 10 5*80 0 10 6*80 0 10
  //   6*80 0 10 6*80 0 10 6*80 0 10 6*80 0 10 6*80 0 10 6*80 0 0 10 5*80 0 0 10 5*80 0 10 22*80 0 10 6*80
  //   0 4 0 10 4*80 0 10 6*80 0 0 10 5*80 0 10 6*80 0 0 10 5*80 0 0 10 5*80 0 4 0 10 4*80 0 4 0 10 4*80 0
  //   0 10 5*80 4 4 14 5*80 0 0 1 10 4*80 0 2 10 5*80 0 0 10 21*80 0 10 6*80 0 7*80 0 10 6*80 0 0 10 5*80
  //   0 10 6*80 0 0 10 5*80 0 0 10 5*80 0 4 0 10 4*80 0 4 0 10 4*80 0 0 10 5*80 4 4 14 5*80 0 0 10 5*80 0
  //   0 10 5*80 0 0 10 21*80 0 10 6*80 0 4 0 10 4*80 0 10 6*80 0 0 10 5*80 0 10 6*80 0 10 6*80 0 10 6*80 0
  //   10 6*80 0 10 6*80 0 10 6*80 4 10 6*80 0 0 10 5*80 0 0 10 5*80 0 10 22*80 0 10 6*80 0 7*80 0 10 6*80
  //   0 0 10 5*80 0 10 6*80 0 10 6*80 0 10 6*80 0 10 6*80 0 10 6*80 0 10 6*80 4 10 6*80 0 0 10 5*80 0 0 10
  //   5*80 0 10 22*80 0 10 6*80 0 4 0 10 4*80 0 10 6*80 0 0 10 5*80 0 10 6*80 0 8 0 10 4*80 0 8 0 10 4*80
  //   0 4 0 10 4*80 0 4 0 10 4*80 0 0 10 5*80 0 0 10 5*80 0 18 6*80 0 18 6*80 0 0 10 21*80 0 10 6*80 0
  //   7*80 0 10 6*80 0 0 10 5*80 0 10 6*80 0 8 0 10 4*80 0 8 0 10 4*80 0 4 0 10 4*80 0 4 0 10 4*80 0 0 10
  //   5*80 0 0 10 5*80 0 18 6*80 0 18 6*80 0 0 10 21*80 0 10 6*80 0 4 0 10 4*80 0 10 6*80 0 0 10 5*80 0 10
  //   6*80 0 10 6*80 0 10 6*80 0 10 6*80 0 10 6*80 0 10 6*80 0 10 6*80 0 0 10 5*80 0 0 10 5*80 0 10 22*80
  //   0 10 6*80 0 7*80 0 10 6*80 0 0 10 5*80 0 10 6*80 0 10 6*80 0 10 6*80 0 10 6*80 0 10 6*80 0 10 6*80 0
  //   10 6*80 0 0 10 5*80 0 0 10 5*80 0 10 22*80 0 10 6*80 0 4 0 10 4*80 0 10 6*80 0 0 10 5*80 0 10 6*80 0
  //   0 10 5*80 0 0 10 5*80 0 0 10 5*80 0 0 10 5*80 0 0 8 30 4*80 4 4 30 5*80 0 0 1 10 4*80 0 2 10 5*80 0
  //   8 30 21*80 0 30 6*80 0 7*80 0 10 6*80 0 0 10 5*80 0 10 6*80 0 0 10 5*80 0 0 10 5*80 0 0 10 5*80 0 0
  //   10 5*80 0 0 8 30 4*80 4 4 30 5*80 0 0 10 5*80 0 0 10 5*80 0 8 30 21*80 0 30 6*80 0 4 0 10 4*80 0 10
  //   6*80 0 0 10 5*80 0 10 6*80 0 10 6*80 0 10 6*80 0 10 6*80 0 10 6*80 0 10 6*80 4 10 6*80 0 0 10 5*80 0
  //   0 10 5*80 0 10 22*80 0 30 6*80 0 7*80 0 10 6*80 0 0 10 5*80 0 10 6*80 0 10 6*80 0 10 6*80 0 10 6*80
  //   0 10 6*80 0 10 6*80 4 10 6*80 0 0 10 5*80 0 0 10 5*80 0 10 22*80 0 30 6*80 0 4 0 10 4*80 0 10 6*80 0
  //   0 10 5*80 0 10 6*80 0 8 0 10 4*80 0 8 0 10 4*80 0 0 10 5*80 0 0 10 5*80 0 0 8 30 4*80 0 0 30 5*80 0
  //   18 6*80 0 18 6*80 0 8 30 21*80 0 30 6*80 0 7*80 0 10 6*80 0 0 10 5*80 0 10 6*80 0 8 0 10 4*80 0 8 0
  //   10 4*80 0 0 10 5*80 0 0 10 5*80 0 0 8 30 4*80 0 0 30 5*80 0 18 6*80 0 18 6*80 0 8 30 21*80 0 30 6*80
  //   0 4 0 10 4*80 0 10 6*80 0 0 10 5*80 0 10 6*80 0 10 6*80 0 10 6*80 0 10 6*80 0 10 6*80 0 10 6*80 0 10
  //   6*80 0 0 10 5*80 0 0 10 5*80 0 10 22*80 0 30 6*80 0 7*80 0 10 6*80 0 0 10 5*80 0 10 6*80 0 10 6*80 0
  //   10 6*80 0 10 6*80 0 10 6*80 0 10 6*80 0 10 6*80 0 0 10 5*80 0 0 10 5*80 0 10 22*80 0 30 6*80 0 4 0
  //   10 4*80 0 10 6*80 0 0 10 5*80 0 10 6*80 0 0 10 5*80 0 0 10 5*80 0 4 0 10 4*80 0 4 0 10 4*80 0 0 8 30
  //   4*80 4 4 30 5*80 0 0 1 10 4*80 0 2 10 5*80 0 8 30 21*80 0 30 6*80 0 7*80 0 10 6*80 0 0 10 5*80 0 10
  //   6*80 0 0 10 5*80 0 0 10 5*80 0 4 0 10 4*80 0 4 0 10 4*80 0 0 8 30 4*80 4 4 30 5*80 0 0 10 5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
endmodule

module ProgramROM (
  input  [15:0] ADDR,
  output [3:0] CMD
);

  wire [7:0] rom_1_data;

  ROM #(.addrWidth(13)) rom_1 (.addr(ADDR[13:1]), .data(rom_1_data));
  Multiplexer multiplexer_1 (.in0(rom_1_data[0]), .in1(rom_1_data[4]), .out(CMD[0]), .sel(ADDR[0]));
  Multiplexer multiplexer_2 (.in0(rom_1_data[1]), .in1(rom_1_data[5]), .out(CMD[1]), .sel(ADDR[0]));
  Multiplexer multiplexer_3 (.in0(rom_1_data[2]), .in1(rom_1_data[6]), .out(CMD[2]), .sel(ADDR[0]));
  Multiplexer multiplexer_4 (.in0(rom_1_data[3]), .in1(rom_1_data[7]), .out(CMD[3]), .sel(ADDR[0]));

  // Notes on the sheet:
  //   contents of rom_1 (hex, n*v repeats v):
  //   12 34 56 78
endmodule

module ClockModule (
  input  CLR,
  input  CLK,
  input  HLT,
  input  RESUME,
  output D_CLK,
  output M_CLK
);

  wire and_1_out, and_2_out, n74161_1_pin3, n74161_1_pin7, n74161_1_pin9, n74161_1_pin10, n74161_1_pin11,
       n74161_1_pin12, n74161_1_pin13, not_1_out, s_r_ff_1_qn, undriven;

  and and_1 (and_1_out, CLK, HLT);
  S_R_Flip_Flop s_r_ff_1 (.S(undriven), .reset(RESUME), .Qn(s_r_ff_1_qn), .preset(and_1_out));  // open: R, clk, Q
  not not_1 (not_1_out, CLR);
  and and_2 (and_2_out, CLK, s_r_ff_1_qn);
  _74161 u_74161_1 (
    .pin1(not_1_out), .pin2(and_2_out), .pin3(n74161_1_pin3), .pin4(n74161_1_pin3), .pin5(n74161_1_pin3),
    .pin6(n74161_1_pin3), .pin7(n74161_1_pin7), .pin14(D_CLK), .pin13(n74161_1_pin13),
    .pin12(n74161_1_pin12), .pin11(n74161_1_pin11), .pin10(n74161_1_pin10), .pin9(n74161_1_pin9));  // open: pin15
  // NoConnect on n74161_1_pin13
  // NoConnect on n74161_1_pin12
  // NoConnect on n74161_1_pin11
  not not_2 (M_CLK, D_CLK);
  // also tied to GND on the sheet: n74161_1_pin3
  // also tied to VCC on the sheet: {n74161_1_pin7, n74161_1_pin10, n74161_1_pin9}
endmodule

module RamModule (
  input  [15:0] ADDR_IN,
  input  WE,
  input  OE,
  input  CLK,
  input  [15:0] DATA_IN,
  output [15:0] DATA_OUT
);

  RAM #(.addrWidth(16), .clearpin("true")) RAM1 (
    .addr(ADDR_IN), .we(WE), .oe(OE), .clk(CLK), .din(DATA_IN[7:0]), .dout(DATA_OUT[7:0]));  // open: clr
  RAM #(.addrWidth(16), .clearpin("true")) RAM2 (
    .addr(ADDR_IN), .we(WE), .oe(OE), .clk(CLK), .din(DATA_IN[15:8]), .dout(DATA_OUT[15:8]));  // open: clr
endmodule

module IOModule (
  input  [7:0] DATA_IN,
  input  CLK,
  input  EN_OUT,
  input  CLR,
  input  CLR_K,
  output K_OUT
);

  TTY tty_1 (.data(DATA_IN[6:0]), .clk(CLK), .we(EN_OUT), .clr(CLR));
  D_Flip_Flop d_ff_1 (.D(EN_OUT), .clk(CLK), .Q(K_OUT), .reset(CLR_K));  // open: Qn, preset
endmodule
