// Logisim project clock_divider.circ as structural Verilog: 1 circuit, main circuit main
module main (
  output LD_0,
  output LD_1,
  output LD_2,
  output CLK_0,
  output CLK_2,
  output CLK_1,
  output CLK
);

  wire n7404_1_pin5, n7408_1_pin1, n7408_1_pin2, n7408_1_pin5, n7408_1_pin9, n7408_1_pin12, n74138_1_pin1,
       n74138_1_pin2, n74138_1_pin4, n74138_1_pin5, n74138_1_pin6, n74138_1_pin11, n74161_1_pin2,
       n74161_1_pin7, n74161_1_pin9, n74161_1_pin10;

  LED led_1 (.in(CLK_0));
  LED led_2 (.in(CLK_1));
  LED led_3 (.in(CLK_2));
  LED led_4 (.in(CLK));
  _7408 u_7408_1 (
    .pin1(n7408_1_pin1), .pin2(n7408_1_pin2), .pin3(CLK_2), .pin4(n7408_1_pin1), .pin5(n7408_1_pin5),
    .pin6(CLK), .pin13(n7408_1_pin1), .pin12(n7408_1_pin12), .pin11(CLK_0), .pin10(n7408_1_pin1),
    .pin9(n7408_1_pin9), .pin8(CLK_1));
  _7404 u_7404_1 (
    .pin5(n7404_1_pin5), .pin6(n7408_1_pin5), .pin13(LD_0), .pin12(n7408_1_pin12), .pin11(LD_1),
    .pin10(n7408_1_pin9), .pin9(LD_2), .pin8(n7408_1_pin2));  // open: pin1, pin2, pin3, pin4
  _74138 u_74138_1 (
    .pin1(n74138_1_pin1), .pin2(n74138_1_pin2), .pin4(n74138_1_pin4), .pin5(n74138_1_pin5),
    .pin6(n74138_1_pin6), .pin15(LD_0), .pin14(LD_1), .pin13(LD_2), .pin12(n7404_1_pin5),
    .pin11(n74138_1_pin11));  // open: pin3, pin7, pin10, pin9
  _74161 u_74161_1 (
    .pin1(n74138_1_pin11), .pin2(n74161_1_pin2), .pin7(n74161_1_pin7), .pin14(n74138_1_pin1),
    .pin13(n74138_1_pin2), .pin10(n74161_1_pin10), .pin9(n74161_1_pin9));  // open: pin3, pin4, pin5, pin6, pin15, pin12, pin11
  not not_1 (n7408_1_pin1, n74161_1_pin2);
  Clock M_CLK (.out(n74161_1_pin2));
  // also tied to GND on the sheet: {n74138_1_pin4, n74138_1_pin5}
  // also tied to VCC on the sheet: {n74138_1_pin6, n74161_1_pin10, n74161_1_pin7, n74161_1_pin9}

  // Notes on the sheet:
  //   CLK 0   1   2   3
endmodule
