// Logisim project counter_circuit_logisim.circ as structural Verilog: 1 circuit, main circuit main
module main (
  input  CE,
  input  CR
);

  wire n74161_1_pin2, n74161_1_pin3, n74161_1_pin9, n74161_1_pin11, n74161_1_pin12, n74161_1_pin13,
       n74161_1_pin14, n74161_1_pin15;

  _74161 #(.ShowInternalStructure("true")) u_74161_1 (
    .pin1(CR), .pin2(n74161_1_pin2), .pin3(n74161_1_pin3), .pin4(n74161_1_pin3), .pin5(n74161_1_pin3),
    .pin6(n74161_1_pin3), .pin7(CE), .pin15(n74161_1_pin15), .pin14(n74161_1_pin14), .pin13(n74161_1_pin13),
    .pin12(n74161_1_pin12), .pin11(n74161_1_pin11), .pin10(CE), .pin9(n74161_1_pin9));
  LED led_1 (.in(n74161_1_pin14));
  LED led_2 (.in(n74161_1_pin13));
  Clock clock_1 (.out(n74161_1_pin2));
  LED led_3 (.in(n74161_1_pin12));
  LED led_4 (.in(n74161_1_pin11));
  // also tied to GND on the sheet: {n74161_1_pin15, n74161_1_pin3}
  // also tied to VCC on the sheet: n74161_1_pin9

  // Notes on the sheet:
  //   no chain = no need
  //   resets the latched value
  //   grounded LEDs
  //   clock
  //   enables edge-triggered counting
endmodule
