// Logisim project ram_driver.circ as structural Verilog: 1 circuit, main circuit main
module main (
  input  CLC,
  input  OE,
  input  WE,
  output x,
  output EN,
  output DIR,
  output nWE,
  output nOE
);

  wire and_1_out, and_2_out, and_3_out, not_1_out, not_2_out;

  not not_1 (not_1_out, OE);
  not not_2 (not_2_out, CLC);
  and and_1 (and_1_out, not_1_out, WE);
  and and_2 (and_2_out, OE, WE);
  and and_3 (and_3_out, not_2_out, and_1_out);
  not not_3 (DIR, WE);
  xor xor_1 (x, and_3_out, and_2_out);
  xor xor_2 (EN, OE, WE);

  assign nOE = WE;
  assign nWE = DIR;

  // Notes on the sheet:
  //   CE#
endmodule
