// Logisim project test.circ as structural Verilog: 1 circuit, main circuit main
module main (
  input  in_1,
  input  CLR
);

  wire clock_1_out, nand_1_out;
  wire [3:0] n74161_1_pin11;

  Clock clock_1 (.out(clock_1_out));
  nand nand_1 (nand_1_out, CLR, clock_1_out);
  _74161 u_74161_1 (
    .pin1(nand_1_out), .pin2(clock_1_out), .pin14(n74161_1_pin11[3]), .pin13(n74161_1_pin11[2]),
    .pin12(n74161_1_pin11[1]), .pin11(n74161_1_pin11[0]), .pin10(in_1));  // open: pin3, pin4, pin5, pin6, pin7, pin15, pin9
  Hex_Digit_Display hex_digit_display_1 (.value(n74161_1_pin11));  // open: dp
endmodule
